// Logisim project CPU.circ as structural Verilog: 8 circuits, main circuit implementation
module implementation (
  input  [15:0] Instruction_In,
  input  ClkIn,
  output [4:0] Instruction_Address_Out,
  output [3:0] Reg0_Out,
  output [3:0] Reg1_Out,
  output [3:0] Reg2_Out,
  output [3:0] Reg3_Out,
  output [3:0] Reg4_Out,
  output [3:0] Reg5_Out,
  output [3:0] Reg6_Out,
  output [3:0] Reg7_Out,
  output [3:0] Reg8_Out,
  output [3:0] Reg9_Out,
  output [3:0] Reg10_Out,
  output [3:0] Reg11_Out,
  output [3:0] Reg12_Out,
  output [3:0] Reg13_Out,
  output [3:0] Reg14_Out,
  output [3:0] Reg15_Out
);

  wire Is_immediate, reg_write, Stop;
  wire [3:0] A_Value, ALU_B, ALU_code, B_Value, data;
  wire [4:0] programcounter_1_next_instruction_address;

  // Probe on Instruction_In[3:0]
  // Probe on Instruction_In[7:4]
  // Probe on Instruction_In[11:8]
  CPU_decoder cpu_decoder_1 (
    .OPCODE(Instruction_In[15:12]), .clock(ClkIn), .ALUOPCODE(ALU_code), .REGWRITE(reg_write),
    .ISIMMEDIATE(Is_immediate), .out_6(Stop));
  Multiplexer #(.enable("false"), .width(4)) multiplexer_1 (
    .in0(B_Value), .in1(Instruction_In[3:0]), .out(ALU_B), .sel(Is_immediate));
  // Probe on Instruction_In[15:12]
  // Probe on ALU_code
  // Probe on data
  ALU alu_1 (.RegA(A_Value), .RegB(ALU_B), .Opcode(ALU_code), .RegC(data));
  RegFile regfile_1 (
    .A_Sel_In(Instruction_In[7:4]), .B_Sel_In(Instruction_In[3:0]), .C_Sel_In(Instruction_In[11:8]),
    .Data_In(data), .Reg_Write_In(reg_write), .clk_in(ClkIn), .A_Out(A_Value), .B_Out(B_Value),
    .Reg0_Out(Reg0_Out), .Reg1_Out(Reg1_Out), .Reg2_Out(Reg2_Out), .Reg3_Out(Reg3_Out), .Reg4_Out(Reg4_Out),
    .Reg5_Out(Reg5_Out), .Reg6_Out(Reg6_Out), .Reg7_Out(Reg7_Out), .Reg8_Out(Reg8_Out), .Reg9_Out(Reg9_Out),
    .Reg10_Out(Reg10_Out), .Reg11_Out(Reg11_Out), .Reg12_Out(Reg12_Out), .Reg13_Out(Reg13_Out),
    .Reg14_Out(Reg14_Out), .Reg15_Out(Reg15_Out));
  ProgramCounter programcounter_1 (
    .instruction_address(Instruction_Address_Out), .stop_on(Stop),
    .next_instruction_address(programcounter_1_next_instruction_address));
  Register #(.width(5)) register_1 (
    .D(programcounter_1_next_instruction_address), .clk(ClkIn), .Q(Instruction_Address_Out));  // open: en, clr

  // Other names for the same wires on the sheet: Clk = ClkIn; Bsel_immediate[3:0] = Instruction_In[3:0];
  //   Instruction[15:0] = Instruction_In; Asel[3:0] = Instruction_In[7:4]; Csel[3:0] = Instruction_In[11:8];
  //   Opcode[3:0] = Instruction_In[15:12]; Instruction_Address[4:0] = Instruction_Address_Out; Reg0[3:0] = Reg0_Out;
  //   Reg1[3:0] = Reg1_Out; Reg2[3:0] = Reg2_Out; Reg3[3:0] = Reg3_Out; Reg4[3:0] = Reg4_Out; Reg5[3:0] = Reg5_Out;
  //   Reg6[3:0] = Reg6_Out; Reg7[3:0] = Reg7_Out; Reg8[3:0] = Reg8_Out; Reg9[3:0] = Reg9_Out; Reg10[3:0] = Reg10_Out;
  //   Reg11[3:0] = Reg11_Out; Reg12[3:0] = Reg12_Out; Reg13[3:0] = Reg13_Out; Reg14[3:0] = Reg14_Out;
  //   Reg15[3:0] = Reg15_Out

  // Notes on the sheet:
  //   Madison Chamberlain
  //   Vivek Goswami
  //   ALU CODE DECODER:
  //   LOAD: 0000
  //   MOVE: 0001
  //   AND: 0010
  //   OR: 0011
  //   XOR: 0100
  //   NOT: 0101
  //   NEGATE: 0110
  //   ADD: 0111
  //   SUB: 1000
endmodule

module RegFile (
  input  [3:0] A_Sel_In,
  input  [3:0] B_Sel_In,
  input  [3:0] C_Sel_In,
  input  [3:0] Data_In,
  input  Reg_Write_In,
  input  clk_in,
  output [3:0] A_Out,
  output [3:0] B_Out,
  output [3:0] Reg0_Out,
  output [3:0] Reg1_Out,
  output [3:0] Reg2_Out,
  output [3:0] Reg3_Out,
  output [3:0] Reg4_Out,
  output [3:0] Reg5_Out,
  output [3:0] Reg6_Out,
  output [3:0] Reg7_Out,
  output [3:0] Reg8_Out,
  output [3:0] Reg9_Out,
  output [3:0] Reg10_Out,
  output [3:0] Reg11_Out,
  output [3:0] Reg12_Out,
  output [3:0] Reg13_Out,
  output [3:0] Reg14_Out,
  output [3:0] Reg15_Out
);

  wire Reg_Write0, Reg_Write1, Reg_Write2, Reg_Write3, Reg_Write4, Reg_Write5, Reg_Write6, Reg_Write7,
       Reg_Write8, Reg_Write9, Reg_Write10, Reg_Write11, Reg_Write12, Reg_Write13, Reg_Write14, Reg_Write15;

  Demultiplexer #(.enable("false"), .select(4)) demultiplexer_1 (
    .out0(Reg_Write0), .out1(Reg_Write1), .out2(Reg_Write2), .out3(Reg_Write3), .out4(Reg_Write4),
    .out5(Reg_Write5), .out6(Reg_Write6), .out7(Reg_Write7), .out8(Reg_Write8), .out9(Reg_Write9),
    .out10(Reg_Write10), .out11(Reg_Write11), .out12(Reg_Write12), .out13(Reg_Write13), .out14(Reg_Write14),
    .out15(Reg_Write15), .in(Reg_Write_In), .sel(C_Sel_In));
  Register #(.width(4)) register_1 (.D(Data_In), .en(Reg_Write0), .clk(clk_in), .Q(Reg0_Out));  // open: clr
  Register #(.width(4)) register_2 (.D(Data_In), .en(Reg_Write4), .clk(clk_in), .Q(Reg4_Out));  // open: clr
  Register #(.width(4)) register_3 (.D(Data_In), .en(Reg_Write8), .clk(clk_in), .Q(Reg8_Out));  // open: clr
  Register #(.width(4)) register_4 (.D(Data_In), .en(Reg_Write12), .clk(clk_in), .Q(Reg12_Out));  // open: clr
  Register #(.width(4)) register_5 (.D(Data_In), .en(Reg_Write1), .clk(clk_in), .Q(Reg1_Out));  // open: clr
  Register #(.width(4)) register_6 (.D(Data_In), .en(Reg_Write5), .clk(clk_in), .Q(Reg5_Out));  // open: clr
  Register #(.width(4)) register_7 (.D(Data_In), .en(Reg_Write9), .clk(clk_in), .Q(Reg9_Out));  // open: clr
  Register #(.width(4)) register_8 (.D(Data_In), .en(Reg_Write13), .clk(clk_in), .Q(Reg13_Out));  // open: clr
  Register #(.width(4)) register_9 (.D(Data_In), .en(Reg_Write2), .clk(clk_in), .Q(Reg2_Out));  // open: clr
  Register #(.width(4)) register_10 (.D(Data_In), .en(Reg_Write6), .clk(clk_in), .Q(Reg6_Out));  // open: clr
  Register #(.width(4)) register_11 (.D(Data_In), .en(Reg_Write10), .clk(clk_in), .Q(Reg10_Out));  // open: clr
  Register #(.width(4)) register_12 (.D(Data_In), .en(Reg_Write14), .clk(clk_in), .Q(Reg14_Out));  // open: clr
  Register #(.width(4)) register_13 (.D(Data_In), .en(Reg_Write3), .clk(clk_in), .Q(Reg3_Out));  // open: clr
  Register #(.width(4)) register_14 (.D(Data_In), .en(Reg_Write7), .clk(clk_in), .Q(Reg7_Out));  // open: clr
  Register #(.width(4)) register_15 (.D(Data_In), .en(Reg_Write11), .clk(clk_in), .Q(Reg11_Out));  // open: clr
  Register #(.width(4)) register_16 (.D(Data_In), .en(Reg_Write15), .clk(clk_in), .Q(Reg15_Out));  // open: clr
  Multiplexer #(.enable("false"), .select(4), .width(4)) multiplexer_1 (
    .in0(Reg0_Out), .in1(Reg1_Out), .in2(Reg2_Out), .in3(Reg3_Out), .in4(Reg4_Out), .in5(Reg5_Out),
    .in6(Reg6_Out), .in7(Reg7_Out), .in8(Reg8_Out), .in9(Reg9_Out), .in10(Reg10_Out), .in11(Reg11_Out),
    .in12(Reg12_Out), .in13(Reg13_Out), .in14(Reg14_Out), .in15(Reg15_Out), .out(A_Out), .sel(A_Sel_In));
  Multiplexer #(.enable("false"), .select(4), .width(4)) multiplexer_2 (
    .in0(Reg0_Out), .in1(Reg1_Out), .in2(Reg2_Out), .in3(Reg3_Out), .in4(Reg4_Out), .in5(Reg5_Out),
    .in6(Reg6_Out), .in7(Reg7_Out), .in8(Reg8_Out), .in9(Reg9_Out), .in10(Reg10_Out), .in11(Reg11_Out),
    .in12(Reg12_Out), .in13(Reg13_Out), .in14(Reg14_Out), .in15(Reg15_Out), .out(B_Out), .sel(B_Sel_In));

  // Other names for the same wires on the sheet: A[3:0] = A_Out; A_Sel[3:0] = A_Sel_In; B[3:0] = B_Out;
  //   B_Sel[3:0] = B_Sel_In; C_Sel[3:0] = C_Sel_In; clk = clk_in; Data[3:0] = Data_In; Reg0[3:0] = Reg0_Out;
  //   Reg1[3:0] = Reg1_Out; Reg2[3:0] = Reg2_Out; Reg3[3:0] = Reg3_Out; Reg4[3:0] = Reg4_Out; Reg5[3:0] = Reg5_Out;
  //   Reg6[3:0] = Reg6_Out; Reg7[3:0] = Reg7_Out; Reg8[3:0] = Reg8_Out; Reg9[3:0] = Reg9_Out; Reg10[3:0] = Reg10_Out;
  //   Reg11[3:0] = Reg11_Out; Reg12[3:0] = Reg12_Out; Reg13[3:0] = Reg13_Out; Reg14[3:0] = Reg14_Out;
  //   Reg15[3:0] = Reg15_Out; Reg_Write = Reg_Write_In
endmodule

module ALU (
  input  [3:0] RegA,
  input  [3:0] RegB,
  input  [3:0] Opcode,
  output [3:0] RegC
);

  wire [3:0] AaddB, AandB, AorB, AsubB, AxorB, isNOT, NEGATE;

  // Probe on RegA
  // Probe on AorB
  // Probe on isNOT
  // Probe on AaddB
  // Probe on AsubB
  assign AandB = RegA & RegB;  // AND_Gate and_1, 4 bits wide
  assign AorB = RegA | RegB;  // OR_Gate or_1, 4 bits wide
  assign isNOT = ~RegA;  // NOT_Gate not_1, 4 bits wide
  Subtractor #(.width(4)) subtractor_1 (.a(4'b0000), .b(RegA), .out(NEGATE));  // open: bin, bout
  assign AxorB = RegA ^ RegB;  // XOR_Gate xor_1, 4 bits wide
  Adder #(.width(4)) adder_1 (.a(RegA), .b(RegB), .out(AaddB));  // open: cin, cout
  Subtractor #(.width(4)) subtractor_2 (.a(RegA), .b(RegB), .out(AsubB));  // open: bin, bout
  Multiplexer #(.enable("false"), .select(4), .width(4)) multiplexer_1 (
    .in0(RegB), .in1(RegA), .in2(AandB), .in3(AorB), .in4(AxorB), .in5(isNOT), .in6(NEGATE), .in7(AaddB),
    .in8(AsubB), .out(RegC), .sel(Opcode));  // open: in9, in10, in11, in12, in13, in14, in15

  // Other names for the same wires on the sheet: C[3:0] = RegC; BorI[3:0] = RegB; loadB[3:0] = RegB; A[3:0] = RegA;
  //   move[3:0] = RegA; opp[3:0] = Opcode

  // Notes on the sheet:
  //   LOAD: 0000
  //   MOVE: 0001
  //   AND: 0010
  //   OR: 0011
  //   XOR: 0100
  //   NOT: 0101
  //   NEGATE: 0110
  //   ADD: 0111
  //   SUB: 1000
endmodule

module CPU_decoder (
  input  [3:0] OPCODE,
  input  clock,
  output [3:0] ALUOPCODE,
  output REGWRITE,
  output ISIMMEDIATE,
  output out_6
);

  wire next_state_circ_1_s_next, register_1_q;

  Register #(.width(1)) register_1 (.D(next_state_circ_1_s_next), .clk(clock), .Q(register_1_q));  // open: en, clr
  next_state_circ next_state_circ_1 (.state(register_1_q), .opcode(OPCODE), .s_next(next_state_circ_1_s_next));
  bits_out bits_out_1 (
    .state(register_1_q), .opcode(OPCODE), .alu_code(ALUOPCODE), .stop(out_6), .reg_write(REGWRITE),
    .is_immediate(ISIMMEDIATE));
  // Probe on ALUOPCODE

  // Other names for the same wires on the sheet: aluout[3:0] = ALUOPCODE; Clk = clock; Immed = ISIMMEDIATE;
  //   op[3:0] = OPCODE; stop = out_6; write = REGWRITE

  // Notes on the sheet:
  //   LOAD: 0000
  //   AND: 0010
  //   XOR: 0100
  //   NOT: 0101
  //   ADD: 0111
  //   SUB: 1000
  //   MOVE: 0001
  //   OR: 0011
  //   NEGATE: 0110
  //   I DID NOT INCLUDE STOP/NOP IN ALU CODE
endmodule

module ProgramCounter (
  input  [4:0] instruction_address,
  input  stop_on,
  output [4:0] next_instruction_address
);

  wire and_1_out, and_2_out, and_3_out, and_4_out, and_5_out, and_6_out, and_7_out, and_8_out, and_9_out,
       and_10_out, and_11_out, and_12_out, and_13_out, and_14_out, and_15_out, and_16_out, and_17_out,
       and_18_out, and_19_out, and_20_out, not_1_out, not_2_out, not_3_out, not_4_out, not_5_out, not_6_out;

  not not_1 (not_1_out, instruction_address[4]);
  not not_2 (not_2_out, instruction_address[3]);
  not not_3 (not_3_out, instruction_address[2]);
  not not_4 (not_4_out, instruction_address[1]);
  not not_5 (not_5_out, instruction_address[0]);
  not not_6 (not_6_out, stop_on);
  and and_1 (and_1_out, not_1_out, instruction_address[3], instruction_address[2], instruction_address[1], instruction_address[0], not_6_out);
  and and_2 (and_2_out, instruction_address[4], not_2_out);
  and and_3 (and_3_out, instruction_address[4], not_3_out);
  and and_4 (and_4_out, instruction_address[4], not_4_out);
  and and_5 (and_5_out, instruction_address[4], not_5_out);
  and and_6 (and_6_out, instruction_address[4], stop_on);
  and and_7 (and_7_out, not_2_out, instruction_address[2], instruction_address[1], instruction_address[0], not_6_out);
  and and_8 (and_8_out, instruction_address[3], not_3_out);
  and and_9 (and_9_out, instruction_address[3], not_4_out);
  and and_10 (and_10_out, instruction_address[3], not_5_out);
  and and_11 (and_11_out, instruction_address[3], stop_on);
  and and_12 (and_12_out, not_3_out, instruction_address[1], instruction_address[0], not_6_out);
  and and_13 (and_13_out, instruction_address[2], not_4_out);
  and and_14 (and_14_out, instruction_address[2], not_5_out);
  and and_15 (and_15_out, instruction_address[2], stop_on);
  and and_16 (and_16_out, not_4_out, instruction_address[0], not_6_out);
  and and_17 (and_17_out, instruction_address[1], not_5_out);
  and and_18 (and_18_out, instruction_address[1], stop_on);
  and and_19 (and_19_out, not_5_out, not_6_out);
  and and_20 (and_20_out, instruction_address[0], stop_on);
  or or_1 (next_instruction_address[3], and_7_out, and_8_out, and_9_out, and_10_out, and_11_out);
  or or_2 (next_instruction_address[2], and_12_out, and_13_out, and_14_out, and_15_out);
  or or_3 (next_instruction_address[1], and_16_out, and_17_out, and_18_out);
  or or_4 (next_instruction_address[0], and_19_out, and_20_out);
  or or_5 (next_instruction_address[4], and_1_out, and_2_out, and_3_out, and_4_out, and_5_out, and_6_out);
endmodule

module next_state (
  input  [4:0] state,
  input  [3:0] opcode,
  output [4:0] next_state
);

  wire and_2_out, and_3_out, and_4_out, and_5_out, and_6_out, and_7_out, and_8_out, and_9_out, and_10_out,
       not_1_out, not_2_out, not_3_out;

  not not_1 (not_1_out, opcode[3]);
  not not_2 (not_2_out, opcode[2]);
  not not_3 (not_3_out, opcode[1]);
  not not_4 (next_state[0], opcode[0]);
  and and_1 (next_state[4], opcode[3], opcode[2], opcode[1], opcode[0]);
  and and_2 (and_2_out, not_1_out, opcode[2], opcode[1], opcode[0]);
  and and_3 (and_3_out, opcode[3], not_2_out);
  and and_4 (and_4_out, opcode[3], not_3_out);
  and and_5 (and_5_out, opcode[3], next_state[0]);
  and and_6 (and_6_out, not_2_out, opcode[1], opcode[0]);
  and and_7 (and_7_out, opcode[2], not_3_out);
  and and_8 (and_8_out, opcode[2], next_state[0]);
  and and_9 (and_9_out, not_3_out, opcode[0]);
  and and_10 (and_10_out, opcode[1], next_state[0]);
  or or_1 (next_state[3], and_2_out, and_3_out, and_4_out, and_5_out);
  or or_2 (next_state[2], and_6_out, and_7_out, and_8_out);
  or or_3 (next_state[1], and_9_out, and_10_out);
endmodule

module bits_out (
  input  state,
  input  [3:0] opcode,
  output [3:0] alu_code,
  output stop,
  output reg_write,
  output is_immediate
);

  wire and_2_out, and_3_out, and_4_out, and_5_out, and_6_out, and_7_out, and_8_out, and_9_out, and_10_out,
       and_12_out, and_13_out, and_14_out, not_1_out, not_2_out, not_3_out, not_4_out;

  not not_1 (not_1_out, opcode[3]);
  not not_2 (not_2_out, opcode[2]);
  not not_3 (not_3_out, opcode[1]);
  not not_4 (not_4_out, opcode[0]);
  and and_1 (alu_code[3], opcode[3], opcode[2], opcode[1]);
  and and_2 (and_2_out, opcode[3], not_2_out);
  and and_3 (and_3_out, opcode[3], not_3_out);
  and and_4 (and_4_out, not_1_out, opcode[2]);
  and and_5 (and_5_out, opcode[2], not_3_out);
  and and_6 (and_6_out, opcode[3], not_2_out, opcode[1], opcode[0]);
  and and_7 (and_7_out, not_1_out, not_2_out, opcode[0]);
  and and_8 (and_8_out, not_1_out, opcode[2], opcode[1]);
  and and_9 (and_9_out, opcode[3], not_2_out, opcode[1], not_4_out);
  and and_10 (and_10_out, opcode[3], opcode[2], not_3_out);
  and and_11 (stop, not_1_out, not_2_out, not_3_out, not_4_out);
  or or_1 (reg_write, opcode[1], opcode[2], opcode[3], state);
  and and_12 (and_12_out, not_1_out, not_2_out, opcode[1], not_4_out);
  and and_13 (and_13_out, opcode[2], opcode[0]);
  and and_14 (and_14_out, opcode[3], not_3_out, opcode[0]);
  or or_2 (alu_code[2], and_2_out, and_3_out);
  or or_3 (alu_code[1], and_4_out, and_5_out, and_6_out);
  or or_4 (alu_code[0], and_7_out, and_8_out, and_9_out, and_10_out);
  or or_5 (is_immediate, and_12_out, and_13_out, and_14_out);
endmodule

module next_state_circ (
  input  state,
  input  [3:0] opcode,
  output s_next
);

  wire not_1_out;

  not not_1 (not_1_out, opcode[0]);
  and and_1 (s_next, state, not_1_out);
endmodule
