// Logisim project Cache.circ as structural Verilog: 5 circuits, main circuit implementation
module implementation (
  input  [9:0] CpuAddressIn,
  input  CpuReadIn,
  input  CpuWriteIn,
  input  [7:0] CpuWriteValueIn,
  input  [31:0] LineFromMemIn,
  input  ClkIn,
  output ReadyOut,
  output DidContainOut,
  output [7:0] ByteReadOut,
  output [7:0] MemAddressOut,
  output MemReadOut,
  output MemWriteOut,
  output [31:0] Line2MemOut
);

  wire Contains0, Contains1, MemRead0, MemRead1, MemWrite0, MemWrite1, Ready0, Ready1;
  wire [7:0] ByteReadOut0, ByteReadOut1;
  wire [31:0] Line2Mem0, Line2Mem1;

  set_circ Set0 (
    .CpuAddressIn(CpuAddressIn), .Clock(ClkIn), .CpuReadIn(CpuReadIn), .CpuWriteIn(CpuWriteIn),
    .CpuWriteValueIn(CpuWriteValueIn), .LineFromMemIn(LineFromMemIn), .SetNum(1'b0), .ContainsOut(Contains0),
    .ByteReadOut(ByteReadOut0), .Line2MemOut(Line2Mem0), .MemReadOut(MemRead0), .MemWriteOut(MemWrite0),
    .ReadyOut(Ready0));
  set_circ Set1 (
    .CpuAddressIn(CpuAddressIn), .Clock(ClkIn), .CpuReadIn(CpuReadIn), .CpuWriteIn(CpuWriteIn),
    .CpuWriteValueIn(CpuWriteValueIn), .LineFromMemIn(LineFromMemIn), .SetNum(1'b1), .ContainsOut(Contains1),
    .ByteReadOut(ByteReadOut1), .Line2MemOut(Line2Mem1), .MemReadOut(MemRead1), .MemWriteOut(MemWrite1),
    .ReadyOut(Ready1));
  Multiplexer #(.enable("false")) multiplexer_1 (
    .in0(Contains0), .in1(Contains1), .out(DidContainOut), .sel(CpuAddressIn[2]));
  Multiplexer #(.enable("false"), .width(8)) multiplexer_2 (
    .in0(ByteReadOut0), .in1(ByteReadOut1), .out(ByteReadOut), .sel(CpuAddressIn[2]));
  Multiplexer #(.enable("false"), .width(32)) multiplexer_3 (
    .in0(Line2Mem0), .in1(Line2Mem1), .out(Line2MemOut), .sel(CpuAddressIn[2]));
  and and_1 (ReadyOut, Ready0, Ready1);
  Multiplexer #(.enable("false")) multiplexer_4 (
    .in0(MemRead0), .in1(MemRead1), .out(MemReadOut), .sel(CpuAddressIn[2]));
  Multiplexer #(.enable("false")) multiplexer_5 (
    .in0(MemWrite0), .in1(MemWrite1), .out(MemWriteOut), .sel(CpuAddressIn[2]));

  assign MemAddressOut = CpuAddressIn[9:2];

  // Other names for the same wires on the sheet: clk = ClkIn; CpuAddress[9:0] = CpuAddressIn;
  //   offset[1:0] = CpuAddressIn[1:0]; CpuRead = CpuReadIn; CpuWrite = CpuWriteIn;
  //   CpuWriteValue[7:0] = CpuWriteValueIn; DidContain = DidContainOut; LineFromMem[31:0] = LineFromMemIn;
  //   MemAddress[7:0] = CpuAddressIn[9:2]; set = CpuAddressIn[2]; tag[6:0] = CpuAddressIn[9:3]; MemRead = MemReadOut;
  //   MemWrite = MemWriteOut; Ready = ReadyOut; ByteRead[7:0] = ByteReadOut; SelectedSetByteRead[7:0] = ByteReadOut;
  //   Line2Mem[31:0] = Line2MemOut; SelectedSetLine2Mem[31:0] = Line2MemOut

  // Notes on the sheet:
  //   Vivek Goswami
  //   Madison Chamberlain
  //   Inputs:
  //   Sets:
  //   Choices:
  //   control
  //   data
  //   data
  //   data
  //   control
  //   control
  //   data
  //   Outputs:
endmodule

module set_circ (
  input  [9:0] CpuAddressIn,
  input  Clock,
  input  CpuReadIn,
  input  CpuWriteIn,
  input  [7:0] CpuWriteValueIn,
  input  [31:0] LineFromMemIn,
  input  SetNum,
  output ContainsOut,
  output [7:0] ByteReadOut,
  output [31:0] Line2MemOut,
  output MemReadOut,
  output MemWriteOut,
  output ReadyOut
);

  wire contains0, contains1, contains2, MemRead0, MemRead1, MemRead2, MemWrite0, MemWrite1, MemWrite2,
       one_greatest, one_gt_0, one_gt_2, Ready0, Ready1, Ready2, two_gt_0, two_gt_1, zero_gt_1, zero_gt_2;
  wire [0:0] WhoIsGreatest;
  wire [1:0] Age0, Age1, Age2, AgeOfWayAccessed, WayAccessed, WayWithHighestAge, WhoContains;
  wire [7:0] ByteRead0, ByteRead1, ByteRead2;
  wire [31:0] Line2Mem0, Line2Mem1, Line2Mem2;

  way_circ way_circ_1 (
    .CpuAddressIn(CpuAddressIn), .Clock(Clock), .CpuReadIn(CpuReadIn), .CpuWriteIn(CpuWriteIn),
    .CpuWriteValueIn(CpuWriteValueIn), .LineFromMemIn(LineFromMemIn), .AgeWayAccessedIn(AgeOfWayAccessed),
    .WayNumIn(2'b00), .SelectedWayIn(WayAccessed), .SetNum(SetNum), .ContainsOut(contains0),
    .ByteReadOut(ByteRead0), .Line2MemOut(Line2Mem0), .AgeOut(Age0), .MemReadOut(MemRead0),
    .MemWriteOut(MemWrite0), .ReadyOut(Ready0));
  way_circ way_circ_2 (
    .CpuAddressIn(CpuAddressIn), .Clock(Clock), .CpuReadIn(CpuReadIn), .CpuWriteIn(CpuWriteIn),
    .CpuWriteValueIn(CpuWriteValueIn), .LineFromMemIn(LineFromMemIn), .AgeWayAccessedIn(AgeOfWayAccessed),
    .WayNumIn(2'b01), .SelectedWayIn(WayAccessed), .SetNum(SetNum), .ContainsOut(contains1),
    .ByteReadOut(ByteRead1), .Line2MemOut(Line2Mem1), .AgeOut(Age1), .MemReadOut(MemRead1),
    .MemWriteOut(MemWrite1), .ReadyOut(Ready1));
  way_circ way_circ_3 (
    .CpuAddressIn(CpuAddressIn), .Clock(Clock), .CpuReadIn(CpuReadIn), .CpuWriteIn(CpuWriteIn),
    .CpuWriteValueIn(CpuWriteValueIn), .LineFromMemIn(LineFromMemIn), .AgeWayAccessedIn(AgeOfWayAccessed),
    .WayNumIn(2'b10), .SelectedWayIn(WayAccessed), .SetNum(SetNum), .ContainsOut(contains2),
    .ByteReadOut(ByteRead2), .Line2MemOut(Line2Mem2), .AgeOut(Age2), .MemReadOut(MemRead2),
    .MemWriteOut(MemWrite2), .ReadyOut(Ready2));
  Comparator #(.width(2)) comparator_1 (.a(Age0), .b(Age1), .gt(zero_gt_1), .lt(one_gt_0));  // open: eq
  Comparator #(.width(2)) comparator_2 (.a(Age1), .b(Age2), .gt(one_gt_2), .lt(two_gt_1));  // open: eq
  Comparator #(.width(2)) comparator_3 (.a(Age0), .b(Age2), .gt(zero_gt_2), .lt(two_gt_0));  // open: eq
  BitFinder #(.width(3)) bitfinder_1 (.in({contains2, contains1, contains0}), .index(WhoContains), .found(ContainsOut));
  Multiplexer #(.enable("false"), .select(2), .width(8)) multiplexer_1 (
    .in0(ByteRead0), .in1(ByteRead1), .in2(ByteRead2), .out(ByteReadOut), .sel(WhoContains));  // open: in3
  Multiplexer #(.enable("false"), .select(2), .width(32)) multiplexer_2 (
    .in0(Line2Mem0), .in1(Line2Mem1), .in2(Line2Mem2), .out(Line2MemOut), .sel(WayAccessed));  // open: in3
  Multiplexer #(.enable("false"), .select(2)) multiplexer_3 (
    .in0(MemRead0), .in1(MemRead1), .in2(MemRead2), .out(MemReadOut), .sel(WayAccessed));  // open: in3
  Multiplexer #(.enable("false"), .select(2)) multiplexer_4 (
    .in0(MemWrite0), .in1(MemWrite1), .in2(MemWrite2), .out(MemWriteOut), .sel(WayAccessed));  // open: in3
  and and_1 (ReadyOut, Ready0, Ready1, Ready2);
  // Probe on WhoContains
  and and_2 (WhoIsGreatest[0], zero_gt_1, zero_gt_2);
  and and_3 (one_greatest, one_gt_0, one_gt_2);
  Multiplexer #(.enable("false"), .width(2)) multiplexer_5 (
    .in0(WayWithHighestAge), .in1(WhoContains), .out(WayAccessed), .sel(ContainsOut));
  // Probe on {one_greatest, WhoIsGreatest[0]}
  // Probe on WayWithHighestAge
  Multiplexer #(.enable("false"), .select(2), .width(2)) multiplexer_6 (
    .in0(2'b10), .in1(2'b01), .in2(2'b00), .out(WayWithHighestAge), .sel({one_greatest, WhoIsGreatest[0]}));  // open: in3
  Multiplexer #(.enable("false"), .select(2), .width(2)) multiplexer_7 (
    .in0(Age0), .in1(Age1), .in2(Age2), .out(AgeOfWayAccessed), .sel(WayAccessed));  // open: in3

  // Other names for the same wires on the sheet: ByteRead[7:0] = ByteReadOut; clk = Clock; contains = ContainsOut;
  //   CpuAddress[9:0] = CpuAddressIn; offset[1:0] = CpuAddressIn[1:0]; set = CpuAddressIn[2];
  //   tag[6:0] = CpuAddressIn[9:3]; CpuRead = CpuReadIn; CpuWrite = CpuWriteIn; CpuWriteValue[7:0] = CpuWriteValueIn;
  //   Line2Mem[31:0] = Line2MemOut; LineFromMem[31:0] = LineFromMemIn; MemRead = MemReadOut; MemWrite = MemWriteOut;
  //   Ready = ReadyOut; set_num = SetNum; zero_greatest = WhoIsGreatest[0]; WhoIsGreatest[1] = one_greatest

  // Notes on the sheet:
  //   Inputs:
  //   Way 1
  //   Ways:
  //   Way 0
  //   Way 2
  //   Choices:
  //   Age Maker:
  //   Outputs:
endmodule

module way_circ (
  input  [9:0] CpuAddressIn,
  input  Clock,
  input  CpuReadIn,
  input  CpuWriteIn,
  input  [7:0] CpuWriteValueIn,
  input  [31:0] LineFromMemIn,
  input  [1:0] AgeWayAccessedIn,
  input  [1:0] WayNumIn,
  input  [1:0] SelectedWayIn,
  input  SetNum,
  output ContainsOut,
  output [7:0] ByteReadOut,
  output [31:0] Line2MemOut,
  output [1:0] AgeOut,
  output MemReadOut,
  output MemWriteOut,
  output ReadyOut
);

  wire and_2_out, and_3_out, and_4_out, and_5_out, and_6_out, and_7_out, and_8_out, and_9_out, and_10_out,
       and_11_out, and_12_out, and_13_out, comparator_1_eq, comparator_2_eq, comparator_3_eq,
       comparator_4_eq, comparator_5_eq, comparator_6_eq, comparator_7_eq, comparator_8_eq, DirtyBit,
       multiplexer_1_out, multiplexer_4_out, not_1_out, not_2_out, not_3_out, not_4_out, or_1_out, or_2_out,
       or_3_out, or_4_out, Set_Way_Match, ValidBit, Write_1_To_Dirty, Write_1_To_Valid, Write_from_CPU_Write,
       Write_To_Age, Write_To_Byte, Write_To_Dirty, Write_To_Tag, Write_To_Valid, Write_Way_To_Age;
  wire [1:0] adder_1_out, comparator_9_gt, multiplexer_5_out, NewAge;
  wire [2:0] fsm_next_state_circ_1_next_state, register_1_q;
  wire [6:0] StoredTag;
  wire [7:0] multiplexer_2_out, multiplexer_3_out, multiplexer_6_out, multiplexer_7_out;

  Comparator #(.width(2)) comparator_1 (.a(SelectedWayIn), .b(WayNumIn), .eq(comparator_1_eq));  // open: gt, lt
  Comparator #(.width(1)) comparator_2 (.a(CpuAddressIn[2]), .b(SetNum), .eq(comparator_2_eq));  // open: gt, lt
  and and_1 (Set_Way_Match, comparator_1_eq, comparator_2_eq);
  Comparator #(.width(2)) comparator_3 (.a(CpuAddressIn[1:0]), .b(2'b00), .eq(comparator_3_eq));  // open: gt, lt
  Comparator #(.width(2)) comparator_4 (.a(CpuAddressIn[1:0]), .b(2'b01), .eq(comparator_4_eq));  // open: gt, lt
  not not_1 (not_1_out, Write_from_CPU_Write);
  not not_2 (not_2_out, Write_from_CPU_Write);
  Comparator #(.width(2)) comparator_5 (.a(CpuAddressIn[1:0]), .b(2'b10), .eq(comparator_5_eq));  // open: gt, lt
  Comparator #(.width(2)) comparator_6 (.a(CpuAddressIn[1:0]), .b(2'b11), .eq(comparator_6_eq));  // open: gt, lt
  and and_2 (and_2_out, Write_To_Byte, Set_Way_Match, not_1_out);
  and and_3 (and_3_out, Set_Way_Match, Write_from_CPU_Write, comparator_3_eq);
  and and_4 (and_4_out, Write_To_Byte, Set_Way_Match, not_2_out);
  and and_5 (and_5_out, Set_Way_Match, Write_from_CPU_Write, comparator_4_eq);
  not not_3 (not_3_out, Write_from_CPU_Write);
  not not_4 (not_4_out, Write_from_CPU_Write);
  and and_6 (and_6_out, Write_To_Valid, Set_Way_Match);
  Comparator #(.width(1)) comparator_7 (.a(CpuAddressIn[2]), .b(SetNum), .eq(comparator_7_eq));  // open: gt, lt
  or or_1 (or_1_out, and_2_out, and_3_out);
  or or_2 (or_2_out, and_4_out, and_5_out);
  and and_7 (and_7_out, Write_To_Byte, Set_Way_Match, not_3_out);
  or or_3 (or_3_out, and_7_out, and_8_out);
  and and_8 (and_8_out, Set_Way_Match, Write_from_CPU_Write, comparator_5_eq);
  and and_9 (and_9_out, Write_To_Byte, Set_Way_Match, not_4_out);
  and and_10 (and_10_out, Set_Way_Match, Write_from_CPU_Write, comparator_6_eq);
  Register #(.width(1)) Valid (.D(multiplexer_1_out), .en(and_6_out), .clk(Clock), .Q(ValidBit));  // open: clr
  Multiplexer #(.enable("false")) multiplexer_1 (
    .in0(1'b0), .in1(1'b1), .out(multiplexer_1_out), .sel(Write_1_To_Valid));
  and and_11 (and_11_out, Set_Way_Match, Write_To_Valid);
  and and_12 (and_12_out, Write_To_Age, comparator_7_eq);
  and and_13 (and_13_out, Write_To_Tag, Set_Way_Match);
  Register BYTE0 (.D(multiplexer_2_out), .en(or_1_out), .clk(Clock), .Q(Line2MemOut[7:0]));  // open: clr
  Multiplexer #(.enable("false"), .width(8)) multiplexer_2 (
    .in0(LineFromMemIn[7:0]), .in1(CpuWriteValueIn), .out(multiplexer_2_out), .sel(Write_from_CPU_Write));
  Register BYTE1 (.D(multiplexer_3_out), .en(or_2_out), .clk(Clock), .Q(Line2MemOut[15:8]));  // open: clr
  Multiplexer #(.enable("false"), .width(8)) multiplexer_3 (
    .in0(LineFromMemIn[15:8]), .in1(CpuWriteValueIn), .out(multiplexer_3_out), .sel(Write_from_CPU_Write));
  or or_4 (or_4_out, and_9_out, and_10_out);
  Register #(.width(1)) Dirty (.D(multiplexer_4_out), .en(and_11_out), .clk(Clock), .Q(DirtyBit));  // open: clr
  Multiplexer #(.enable("false")) multiplexer_4 (
    .in0(1'b0), .in1(1'b1), .out(multiplexer_4_out), .sel(Write_1_To_Dirty));
  Register #(.width(2)) AgeR (.D(multiplexer_5_out), .en(and_12_out), .clk(Clock), .Q(AgeOut));  // open: clr
  Multiplexer #(.enable("false"), .width(2)) multiplexer_5 (
    .in0(NewAge), .in1(WayNumIn), .out(multiplexer_5_out), .sel(Write_Way_To_Age));
  Register #(.width(7)) TagR (.D(CpuAddressIn[9:3]), .en(and_13_out), .clk(Clock), .Q(StoredTag));  // open: clr
  Register BYTE2 (.D(multiplexer_6_out), .en(or_3_out), .clk(Clock), .Q(Line2MemOut[23:16]));  // open: clr
  Multiplexer #(.enable("false"), .width(8)) multiplexer_6 (
    .in0(LineFromMemIn[23:16]), .in1(CpuWriteValueIn), .out(multiplexer_6_out), .sel(Write_from_CPU_Write));
  Register BYTE3 (.D(multiplexer_7_out), .en(or_4_out), .clk(Clock), .Q(Line2MemOut[31:24]));  // open: clr
  Multiplexer #(.enable("false"), .width(8)) multiplexer_7 (
    .in0(LineFromMemIn[31:24]), .in1(CpuWriteValueIn), .out(multiplexer_7_out), .sel(Write_from_CPU_Write));
  Comparator #(.width(7)) comparator_8 (.a(CpuAddressIn[9:3]), .b(StoredTag), .eq(comparator_8_eq));  // open: gt, lt
  Adder #(.width(2)) adder_1 (.a(AgeOut), .b(2'b01), .out(adder_1_out));  // open: cin, cout
  and and_14 (ContainsOut, comparator_8_eq, ValidBit);
  Multiplexer #(.enable("false"), .select(2), .width(8)) multiplexer_8 (
    .in0(Line2MemOut[7:0]), .in1(Line2MemOut[15:8]), .in2(Line2MemOut[23:16]), .in3(Line2MemOut[31:24]),
    .out(ByteReadOut), .sel(CpuAddressIn[1:0]));
  // Probe on comparator_9_gt
  Comparator #(.width(2)) comparator_9 (
    .a(AgeWayAccessedIn), .b(AgeOut), .gt(comparator_9_gt[0]), .eq(comparator_9_gt[1]));  // open: lt
  Multiplexer #(.enable("false"), .select(2), .width(2)) multiplexer_9 (
    .in0(AgeOut), .in1(adder_1_out), .in2(2'b00), .out(NewAge), .sel(comparator_9_gt));  // open: in3
  FSM_next_state_circ fsm_next_state_circ_1 (
    .State(register_1_q), .Read(CpuReadIn), .Write(CpuWriteIn), .Way_contains(ContainsOut),
    .Way_dirty(DirtyBit), .Next_State(fsm_next_state_circ_1_next_state));
  Register #(.width(3)) register_1 (
    .D(fsm_next_state_circ_1_next_state), .clk(Clock), .Q(register_1_q));  // open: en, clr
  FSM_bits_out_circ fsm_bits_out_circ_1 (
    .State(register_1_q), .Write_to_byte(Write_To_Byte), .Write_to_byte_write(Write_from_CPU_Write),
    .Write_to_valid(Write_To_Valid), .Write_1_to_valid(Write_1_To_Valid), .Write_to_dirty(Write_To_Dirty),
    .Write_1_to_dirty(Write_1_To_Dirty), .Write_to_age(Write_To_Age), .Write_way_to_age(Write_Way_To_Age),
    .Write_to_tag(Write_To_Tag), .memRead_on(MemReadOut), .memWrite_on(MemWriteOut), .Ready(ReadyOut));

  // Other names for the same wires on the sheet: Age[1:0] = AgeOut; AgeWayAccessed[1:0] = AgeWayAccessedIn;
  //   ByteRead[7:0] = ByteReadOut; clk = Clock; contains = ContainsOut; CpuAddress[9:0] = CpuAddressIn;
  //   offset[1:0] = CpuAddressIn[1:0]; set = CpuAddressIn[2]; tag[6:0] = CpuAddressIn[9:3]; CpuRead = CpuReadIn;
  //   CpuWrite = CpuWriteIn; CpuWriteValue[7:0] = CpuWriteValueIn; Line2Mem[31:0] = Line2MemOut;
  //   LineMem0[7:0] = Line2MemOut[7:0]; LineMem1[7:0] = Line2MemOut[15:8]; LineMem2[7:0] = Line2MemOut[23:16];
  //   LineMem3[7:0] = Line2MemOut[31:24]; LineFromMem[31:0] = LineFromMemIn; LineFromMem0[7:0] = LineFromMemIn[7:0];
  //   LineFromMem1[7:0] = LineFromMemIn[15:8]; LineFromMem2[7:0] = LineFromMemIn[23:16];
  //   LineFromMem3[7:0] = LineFromMemIn[31:24]; MemRead = MemReadOut; MemWrite = MemWriteOut; Ready = ReadyOut;
  //   SelectedWayNum[1:0] = SelectedWayIn; set_num = SetNum; WayNum[1:0] = WayNumIn

  // Notes on the sheet:
  //   Data Splitters:
  //   Inputs:
  //   Registers:
  //   Choices:
  //   FSM:
  //   Outputs:
endmodule

module FSM_next_state_circ (
  input  [2:0] State,
  input  Read,
  input  Write,
  input  Way_contains,
  input  Way_dirty,
  output [2:0] Next_State
);

  wire and_1_out, and_2_out, and_3_out, and_4_out, and_5_out, and_6_out, and_7_out, and_8_out, and_9_out,
       and_10_out, not_1_out, not_2_out, not_3_out, not_4_out, not_5_out, not_6_out, not_7_out;

  not not_1 (not_1_out, State[2]);
  not not_2 (not_2_out, State[1]);
  not not_3 (not_3_out, State[0]);
  not not_4 (not_4_out, Read);
  not not_5 (not_5_out, Write);
  not not_6 (not_6_out, Way_contains);
  not not_7 (not_7_out, Way_dirty);
  and and_1 (and_1_out, not_1_out, not_2_out, State[0], not_4_out, Write);
  or or_1 (Next_State[2], and_1_out, and_2_out);
  and and_2 (and_2_out, not_1_out, not_2_out, State[0], Read, not_5_out, not_6_out, not_7_out);
  and and_3 (and_3_out, not_1_out, not_2_out, State[0], not_4_out, Write, not_7_out);
  and and_4 (and_4_out, not_1_out, not_2_out, State[0], not_4_out, Write, Way_contains);
  and and_5 (and_5_out, not_1_out, not_2_out, State[0], Read, not_5_out, Way_dirty);
  and and_6 (and_6_out, not_1_out, not_2_out, State[0], Read, not_5_out, Way_contains);
  and and_7 (and_7_out, not_4_out, not_5_out);
  and and_8 (and_8_out, not_6_out, Way_dirty);
  and and_9 (and_9_out, not_4_out, Way_contains);
  and and_10 (and_10_out, Read, Write);
  or or_2 (Next_State[1], and_3_out, and_4_out, and_5_out, and_6_out);
  or or_3 (Next_State[0], not_3_out, and_7_out, and_8_out, and_9_out, and_10_out, State[1], State[2]);
endmodule

module FSM_bits_out_circ (
  input  [2:0] State,
  output Write_to_byte,
  output Write_to_byte_write,
  output Write_to_valid,
  output Write_1_to_valid,
  output Write_to_dirty,
  output Write_1_to_dirty,
  output Write_to_age,
  output Write_way_to_age,
  output Write_to_tag,
  output memRead_on,
  output memWrite_on,
  output Ready
);

  wire and_1_out, and_2_out, and_3_out, and_4_out, and_5_out, and_6_out, and_7_out, and_8_out, and_10_out,
       and_11_out, and_12_out, and_13_out, and_14_out, and_15_out, and_16_out, and_17_out, not_1_out,
       not_2_out, not_3_out;

  not not_1 (not_1_out, State[2]);
  not not_2 (not_2_out, State[1]);
  not not_3 (not_3_out, State[0]);
  and and_1 (and_1_out, not_2_out, not_3_out);
  and and_2 (and_2_out, State[1], State[0]);
  and and_3 (and_3_out, State[2], State[0]);
  and and_4 (and_4_out, State[2], State[1]);
  or or_1 (Write_to_valid, not_3_out, State[1], State[2]);
  or or_2 (Write_1_to_valid, State[1], State[2]);
  and and_5 (and_5_out, not_2_out, not_3_out);
  and and_6 (and_6_out, State[1], State[0]);
  and and_7 (and_7_out, State[2], State[0]);
  and and_8 (and_8_out, State[2], State[1]);
  or or_3 (Write_to_age, not_3_out, State[1], State[2]);
  and and_9 (Write_way_to_age, not_1_out, not_2_out, not_3_out);
  and and_10 (and_10_out, not_1_out, State[1], State[0]);
  and and_11 (and_11_out, State[2], not_2_out);
  and and_12 (and_12_out, State[2], not_3_out);
  and and_13 (and_13_out, not_1_out, State[1], State[0]);
  and and_14 (and_14_out, State[2], not_2_out);
  and and_15 (and_15_out, State[2], not_3_out);
  and and_16 (and_16_out, not_1_out, State[1], State[0]);
  and and_17 (and_17_out, State[2], not_2_out, State[0]);
  and and_18 (Ready, not_1_out, not_2_out, State[0]);
  or or_4 (Write_to_byte, and_1_out, and_2_out, State[2]);
  or or_5 (Write_to_byte_write, and_3_out, and_4_out);
  or or_6 (Write_to_dirty, and_5_out, and_6_out, State[2]);
  or or_7 (Write_1_to_dirty, and_7_out, and_8_out);
  or or_8 (Write_to_tag, and_10_out, and_11_out, and_12_out);
  or or_9 (memRead_on, and_13_out, and_14_out, and_15_out);
  or or_10 (memWrite_on, and_16_out, and_17_out);
endmodule
