// Logisim project Cache_TD.circ as structural Verilog: 5 circuits, main circuit implementation
module implementation (
  input  [9:0] CpuAddressIn,
  input  CpuReadIn,
  input  CpuWriteIn,
  input  [7:0] CpuWriteValueIn,
  input  [31:0] LineFromMemIn,
  input  ClkIn,
  output ReadyOut,
  output DidContainOut,
  output [7:0] ByteReadOut,
  output [7:0] MemAddressOut,
  output MemReadOut,
  output MemWriteOut,
  output [31:0] Line2MemOut
);

  wire Contains0, Contains1, CpuWrite0, CpuWrite1, Dirty, Dirty0, Dirty1, Init, UpdateAge, WriteByte,
       WriteByte0, WriteByte1, WriteCPU;
  wire [2:0] fsm_next_state_circ_1_next_state, register_1_q;
  wire [7:0] ByteReadOut0, ByteReadOut1;
  wire [31:0] Line2Mem0, Line2Mem1;

  Demultiplexer #(.enable("false")) demultiplexer_1 (
    .out0(CpuWrite0), .out1(CpuWrite1), .in(WriteCPU), .sel(CpuAddressIn[2]));
  Demultiplexer #(.enable("false")) demultiplexer_2 (
    .out0(WriteByte0), .out1(WriteByte1), .in(WriteByte), .sel(CpuAddressIn[2]));
  Register #(.width(3)) register_1 (
    .D(fsm_next_state_circ_1_next_state), .clk(ClkIn), .Q(register_1_q));  // open: en, clr
  FSM_next_state_circ fsm_next_state_circ_1 (
    .State(register_1_q), .Read(CpuReadIn), .Write(CpuWriteIn), .Way_contains(DidContainOut),
    .Way_dirty(Dirty), .Next_State(fsm_next_state_circ_1_next_state));
  FSM_bits_out_circ fsm_bits_out_circ_1 (
    .State(register_1_q), .memWrite(MemWriteOut), .memRead(MemReadOut), .writeByte(WriteByte),
    .ready(ReadyOut), .init(Init), .updateAge(UpdateAge), .WriteByteFromCPUWrite(WriteCPU));
  set_circ Set0 (
    .CpuAddressIn(CpuAddressIn), .Clock(ClkIn), .CpuWriteIn(CpuWrite0), .CpuWriteValueIn(CpuWriteValueIn),
    .LineFromMemIn(LineFromMemIn), .WriteByte_In(WriteByte0), .Init_in(Init), .Update_Age_In(UpdateAge),
    .writeCPU(WriteCPU), .ContainsOut(Contains0), .ByteReadOut(ByteReadOut0), .Line2MemOut(Line2Mem0),
    .Dirty_Out(Dirty0));
  set_circ Set1 (
    .CpuAddressIn(CpuAddressIn), .Clock(ClkIn), .CpuWriteIn(CpuWrite1), .CpuWriteValueIn(CpuWriteValueIn),
    .LineFromMemIn(LineFromMemIn), .WriteByte_In(WriteByte1), .Init_in(Init), .Update_Age_In(UpdateAge),
    .writeCPU(WriteCPU), .ContainsOut(Contains1), .ByteReadOut(ByteReadOut1), .Line2MemOut(Line2Mem1),
    .Dirty_Out(Dirty1));
  Multiplexer #(.enable("false")) multiplexer_1 (
    .in0(Contains0), .in1(Contains1), .out(DidContainOut), .sel(CpuAddressIn[2]));
  Multiplexer #(.enable("false"), .width(8)) multiplexer_2 (
    .in0(ByteReadOut0), .in1(ByteReadOut1), .out(ByteReadOut), .sel(CpuAddressIn[2]));
  Multiplexer #(.enable("false"), .width(32)) multiplexer_3 (
    .in0(Line2Mem0), .in1(Line2Mem1), .out(Line2MemOut), .sel(CpuAddressIn[2]));
  Multiplexer #(.enable("false")) multiplexer_4 (.in0(Dirty0), .in1(Dirty1), .out(Dirty), .sel(CpuAddressIn[2]));

  assign MemAddressOut = CpuAddressIn[9:2];

  // Other names for the same wires on the sheet: clk = ClkIn; CpuAddress[9:0] = CpuAddressIn;
  //   offset[1:0] = CpuAddressIn[1:0]; CpuRead = CpuReadIn; CpuWrite = CpuWriteIn;
  //   CpuWriteValue[7:0] = CpuWriteValueIn; DidContain = DidContainOut; LineFromMem[31:0] = LineFromMemIn;
  //   MemAddress[7:0] = CpuAddressIn[9:2]; set = CpuAddressIn[2]; tag[6:0] = CpuAddressIn[9:3]; MemRead = MemReadOut;
  //   MemWrite = MemWriteOut; Ready = ReadyOut; ByteRead[7:0] = ByteReadOut; SelectedSetByteRead[7:0] = ByteReadOut;
  //   Line2Mem[31:0] = Line2MemOut; SelectedSetLine2Mem[31:0] = Line2MemOut

  // Notes on the sheet:
  //   Madison Chamberlain
  //   Vivek Goswami
  //   Splitters:
  //   Inputs:
  //   FSM:
  //   Sets:
  //   Choices:
  //   Outputs:
endmodule

module set_circ (
  input  [9:0] CpuAddressIn,
  input  Clock,
  input  CpuWriteIn,
  input  [7:0] CpuWriteValueIn,
  input  [31:0] LineFromMemIn,
  input  WriteByte_In,
  input  Init_in,
  input  Update_Age_In,
  input  writeCPU,
  output ContainsOut,
  output [7:0] ByteReadOut,
  output [31:0] Line2MemOut,
  output Dirty_Out
);

  wire contains0, contains1, contains2, CpuWrite0, CpuWrite1, CpuWrite2, Dirty0, Dirty1, Dirty2,
       one_greatest, one_gt_0, one_gt_2, two_gt_0, two_gt_1, WriteByte0, WriteByte1, WriteByte2, zero_gt_1,
       zero_gt_2;
  wire [0:0] WhoIsGreatest;
  wire [1:0] Age0, Age1, Age2, AgeOfWayAccessed, WayAccessed, WayWithHighestAge, WhoContains;
  wire [7:0] ByteRead0, ByteRead1, ByteRead2;
  wire [31:0] Line2Mem0, Line2Mem1, Line2Mem2;

  Demultiplexer #(.enable("false"), .select(2)) demultiplexer_1 (
    .out0(CpuWrite0), .out1(CpuWrite1), .out2(CpuWrite2), .in(writeCPU), .sel(WayAccessed));  // open: out3
  Demultiplexer #(.enable("false"), .select(2)) demultiplexer_2 (
    .out0(WriteByte0), .out1(WriteByte1), .out2(WriteByte2), .in(WriteByte_In), .sel(WayAccessed));  // open: out3
  way_circ Way0 (
    .CpuAddressIn(CpuAddressIn), .Clock(Clock), .CpuWriteIn(CpuWrite0), .CpuWriteValueIn(CpuWriteValueIn),
    .LineFromMemIn(LineFromMemIn), .AgeWayAccessedIn(AgeOfWayAccessed), .WriteByte_In(WriteByte0),
    .Init_in(Init_in), .Update_Age_In(Update_Age_In), .in_10(writeCPU), .ContainsOut(contains0),
    .ByteReadOut(ByteRead0), .Line2MemOut(Line2Mem0), .AgeOut(Age0), .DirtyOut(Dirty0));
  way_circ Way1 (
    .CpuAddressIn(CpuAddressIn), .Clock(Clock), .CpuWriteIn(CpuWrite1), .CpuWriteValueIn(CpuWriteValueIn),
    .LineFromMemIn(LineFromMemIn), .AgeWayAccessedIn(AgeOfWayAccessed), .WriteByte_In(WriteByte1),
    .Init_in(Init_in), .Update_Age_In(Update_Age_In), .in_10(writeCPU), .ContainsOut(contains1),
    .ByteReadOut(ByteRead1), .Line2MemOut(Line2Mem1), .AgeOut(Age1), .DirtyOut(Dirty1));
  way_circ Way2 (
    .CpuAddressIn(CpuAddressIn), .Clock(Clock), .CpuWriteIn(CpuWrite2), .CpuWriteValueIn(CpuWriteValueIn),
    .LineFromMemIn(LineFromMemIn), .AgeWayAccessedIn(AgeOfWayAccessed), .WriteByte_In(WriteByte2),
    .Init_in(Init_in), .Update_Age_In(Update_Age_In), .in_10(writeCPU), .ContainsOut(contains2),
    .ByteReadOut(ByteRead2), .Line2MemOut(Line2Mem2), .AgeOut(Age2), .DirtyOut(Dirty2));
  Comparator #(.width(2)) comparator_1 (.a(Age0), .b(Age1), .gt(zero_gt_1), .lt(one_gt_0));  // open: eq
  Comparator #(.width(2)) comparator_2 (.a(Age1), .b(Age2), .gt(one_gt_2), .lt(two_gt_1));  // open: eq
  Comparator #(.width(2)) comparator_3 (.a(Age0), .b(Age2), .gt(zero_gt_2), .lt(two_gt_0));  // open: eq
  BitFinder #(.width(3)) bitfinder_1 (.in({contains2, contains1, contains0}), .index(WhoContains), .found(ContainsOut));
  Multiplexer #(.enable("false"), .select(2), .width(8)) multiplexer_1 (
    .in0(ByteRead0), .in1(ByteRead1), .in2(ByteRead2), .out(ByteReadOut), .sel(WhoContains));  // open: in3
  Multiplexer #(.enable("false"), .select(2), .width(32)) multiplexer_2 (
    .in0(Line2Mem0), .in1(Line2Mem1), .in2(Line2Mem2), .out(Line2MemOut), .sel(WhoContains));  // open: in3
  Multiplexer #(.enable("false"), .select(2)) multiplexer_3 (
    .in0(Dirty0), .in1(Dirty1), .in2(Dirty2), .out(Dirty_Out), .sel(WhoContains));  // open: in3
  Multiplexer #(.enable("false"), .width(2)) multiplexer_4 (
    .in0(WayWithHighestAge), .in1(WhoContains), .out(WayAccessed), .sel(ContainsOut));
  and and_1 (WhoIsGreatest[0], zero_gt_1, zero_gt_2);
  and and_2 (one_greatest, one_gt_0, one_gt_2);
  // Probe on {one_greatest, WhoIsGreatest[0]}
  // Probe on WayWithHighestAge
  Multiplexer #(.enable("false"), .select(2), .width(2)) multiplexer_5 (
    .in0(2'b10), .in1(2'b01), .in2(2'b00), .out(WayWithHighestAge), .sel({one_greatest, WhoIsGreatest[0]}));  // open: in3
  Multiplexer #(.enable("false"), .select(2), .width(2)) multiplexer_6 (
    .in0(Age0), .in1(Age1), .in2(Age2), .out(AgeOfWayAccessed), .sel(WayAccessed));  // open: in3

  // Other names for the same wires on the sheet: ByteRead[7:0] = ByteReadOut; clk = Clock; contains = ContainsOut;
  //   CpuAddress[9:0] = CpuAddressIn; offset[1:0] = CpuAddressIn[1:0]; set = CpuAddressIn[2];
  //   tag[6:0] = CpuAddressIn[9:3]; CpuWrite = CpuWriteIn; CpuWriteValue[7:0] = CpuWriteValueIn; Dirty = Dirty_Out;
  //   Init = Init_in; Line2Mem[31:0] = Line2MemOut; LineFromMem[31:0] = LineFromMemIn; UpdateAge = Update_Age_In;
  //   zero_greatest = WhoIsGreatest[0]; WhoIsGreatest[1] = one_greatest; WriteByte = WriteByte_In

  // Notes on the sheet:
  //   Inputs:
  //   Splitters:
  //   Ways:
  //   Choices:
  //   Age Maker:
  //   Outputs:
endmodule

module way_circ (
  input  [9:0] CpuAddressIn,
  input  Clock,
  input  CpuWriteIn,
  input  [7:0] CpuWriteValueIn,
  input  [31:0] LineFromMemIn,
  input  [1:0] AgeWayAccessedIn,
  input  WriteByte_In,
  input  Init_in,
  input  Update_Age_In,
  input  in_10,
  output ContainsOut,
  output [7:0] ByteReadOut,
  output [31:0] Line2MemOut,
  output [1:0] AgeOut,
  output DirtyOut
);

  wire comparator_1_eq, CpuWrite0, CpuWrite1, CpuWrite2, CpuWrite3, multiplexer_6_out, ValidBit;
  wire [1:0] adder_1_out, comparator_2_gt, multiplexer_3_out, NewAge, WayNum;
  wire [6:0] StoredTag;
  wire [7:0] multiplexer_1_out, multiplexer_2_out, multiplexer_4_out, multiplexer_5_out;

  Demultiplexer #(.enable("false"), .select(2)) demultiplexer_1 (
    .out0(CpuWrite0), .out1(CpuWrite1), .out2(CpuWrite2), .out3(CpuWrite3), .in(in_10),
    .sel(CpuAddressIn[1:0]));
  Multiplexer #(.enable("false"), .width(8)) multiplexer_1 (
    .in0(LineFromMemIn[7:0]), .in1(CpuWriteValueIn), .out(multiplexer_1_out), .sel(CpuWrite0));
  Multiplexer #(.enable("false"), .width(8)) multiplexer_2 (
    .in0(LineFromMemIn[31:24]), .in1(CpuWriteValueIn), .out(multiplexer_2_out), .sel(CpuWrite3));
  Multiplexer #(.enable("false"), .width(2)) multiplexer_3 (
    .in0(NewAge), .in1(WayNum), .out(multiplexer_3_out), .sel(Init_in));
  Register BYTE0 (.D(multiplexer_1_out), .en(WriteByte_In), .clk(Clock), .Q(Line2MemOut[7:0]));  // open: clr
  Register BYTE1 (.D(multiplexer_4_out), .en(WriteByte_In), .clk(Clock), .Q(Line2MemOut[15:8]));  // open: clr
  Multiplexer #(.enable("false"), .width(8)) multiplexer_4 (
    .in0(LineFromMemIn[15:8]), .in1(CpuWriteValueIn), .out(multiplexer_4_out), .sel(CpuWrite1));
  Register BYTE2 (.D(multiplexer_5_out), .en(WriteByte_In), .clk(Clock), .Q(Line2MemOut[23:16]));  // open: clr
  Multiplexer #(.enable("false"), .width(8)) multiplexer_5 (
    .in0(LineFromMemIn[23:16]), .in1(CpuWriteValueIn), .out(multiplexer_5_out), .sel(CpuWrite2));
  Register BYTE3 (.D(multiplexer_2_out), .en(WriteByte_In), .clk(Clock), .Q(Line2MemOut[31:24]));  // open: clr
  Register #(.width(1)) Valid (.D(WriteByte_In), .en(WriteByte_In), .clk(Clock), .Q(ValidBit));  // open: clr
  Register #(.width(1)) Dirty (.D(multiplexer_6_out), .en(WriteByte_In), .clk(Clock), .Q(DirtyOut));  // open: clr
  Multiplexer #(.enable("false")) multiplexer_6 (.in0(1'b0), .in1(1'b1), .out(multiplexer_6_out), .sel(CpuWriteIn));
  Register #(.width(2)) Age_R (.D(multiplexer_3_out), .en(Update_Age_In), .clk(Clock), .Q(AgeOut));  // open: clr
  Register #(.width(7)) Tags (.D(CpuAddressIn[9:3]), .en(WriteByte_In), .clk(Clock), .Q(StoredTag));  // open: clr
  Comparator #(.width(7)) comparator_1 (.a(CpuAddressIn[9:3]), .b(StoredTag), .eq(comparator_1_eq));  // open: gt, lt
  and and_1 (ContainsOut, comparator_1_eq, ValidBit);
  Multiplexer #(.enable("false"), .select(2), .width(8)) multiplexer_7 (
    .in0(Line2MemOut[7:0]), .in1(Line2MemOut[15:8]), .in2(Line2MemOut[23:16]), .in3(Line2MemOut[31:24]),
    .out(ByteReadOut), .sel(CpuAddressIn[1:0]));
  Comparator #(.width(2)) comparator_2 (
    .a(AgeWayAccessedIn), .b(AgeOut), .gt(comparator_2_gt[0]), .eq(comparator_2_gt[1]));  // open: lt
  Adder #(.width(2)) adder_1 (.a(AgeOut), .b(2'b01), .out(adder_1_out));  // open: cin, cout
  Multiplexer #(.enable("false"), .select(2), .width(2)) multiplexer_8 (
    .in0(AgeOut), .in1(adder_1_out), .in2(2'b00), .out(NewAge), .sel(comparator_2_gt));  // open: in3

  // Other names for the same wires on the sheet: Age[1:0] = AgeOut; AgeWayAccessed[1:0] = AgeWayAccessedIn;
  //   ByteRead[7:0] = ByteReadOut; clk = Clock; contains = ContainsOut; CpuAddress[9:0] = CpuAddressIn;
  //   offset[1:0] = CpuAddressIn[1:0]; set = CpuAddressIn[2]; tag[6:0] = CpuAddressIn[9:3]; CpuWrite = CpuWriteIn;
  //   CpuWriteValue[7:0] = CpuWriteValueIn; DirtyBit = DirtyOut; Init = Init_in; Line2Mem[31:0] = Line2MemOut;
  //   LineMem0[7:0] = Line2MemOut[7:0]; LineMem1[7:0] = Line2MemOut[15:8]; LineMem2[7:0] = Line2MemOut[23:16];
  //   LineMem3[7:0] = Line2MemOut[31:24]; LineFromMem[31:0] = LineFromMemIn; LineFromMem0[7:0] = LineFromMemIn[7:0];
  //   LineFromMem1[7:0] = LineFromMemIn[15:8]; LineFromMem2[7:0] = LineFromMemIn[23:16];
  //   LineFromMem3[7:0] = LineFromMemIn[31:24]; UpdateAge = Update_Age_In; WriteByte = WriteByte_In; WriteCPU = in_10

  // Notes on the sheet:
  //   Data Splitters:
  //   Inputs:
  //   Registers:
  //   Choices:
  //   Outputs:
endmodule

module FSM_next_state_circ (
  input  [2:0] State,
  input  Read,
  input  Write,
  input  Way_contains,
  input  Way_dirty,
  output [2:0] Next_State
);

  wire and_1_out, and_2_out, and_3_out, and_4_out, and_5_out, and_6_out, and_7_out, and_8_out, and_9_out,
       and_10_out, and_11_out, and_12_out, and_13_out, not_1_out, not_2_out, not_3_out, not_4_out, not_5_out,
       not_6_out, not_7_out;

  not not_1 (not_1_out, State[2]);
  not not_2 (not_2_out, State[1]);
  not not_3 (not_3_out, State[0]);
  not not_4 (not_4_out, Read);
  not not_5 (not_5_out, Write);
  not not_6 (not_6_out, Way_contains);
  not not_7 (not_7_out, Way_dirty);
  and and_1 (and_1_out, not_1_out, not_2_out, State[0], not_4_out, Write);
  and and_2 (and_2_out, not_1_out, not_2_out, State[0], Read, not_5_out, not_6_out, Way_dirty);
  or or_1 (Next_State[2], and_1_out, and_2_out, and_3_out);
  and and_3 (and_3_out, State[2], State[1]);
  and and_4 (and_4_out, State[0], not_4_out, Write, not_6_out);
  and and_5 (and_5_out, State[0], Read, not_5_out, not_7_out);
  and and_6 (and_6_out, State[0], Read, not_5_out, Way_contains);
  and and_7 (and_7_out, State[1], State[0]);
  and and_8 (and_8_out, State[2], not_2_out);
  and and_9 (and_9_out, not_1_out, not_2_out, not_4_out, not_5_out);
  and and_10 (and_10_out, not_1_out, not_2_out, not_5_out, not_6_out, not_7_out);
  and and_11 (and_11_out, not_1_out, not_2_out, not_4_out, Way_dirty);
  and and_12 (and_12_out, not_1_out, not_2_out, not_4_out, Way_contains);
  and and_13 (and_13_out, not_1_out, not_2_out, Read, Write);
  or or_2 (Next_State[1], and_4_out, and_5_out, and_6_out, and_7_out, and_8_out);
  or or_3 (Next_State[0], and_9_out, and_10_out, not_3_out, and_11_out, and_12_out, and_13_out);
endmodule

module FSM_bits_out_circ (
  input  [2:0] State,
  output memWrite,
  output memRead,
  output writeByte,
  output ready,
  output init,
  output updateAge,
  output WriteByteFromCPUWrite
);

  wire and_1_out, and_2_out, and_3_out, and_4_out, and_5_out, and_6_out, and_7_out, and_8_out, and_11_out,
       and_12_out, and_13_out, not_1_out, not_2_out, not_3_out;

  not not_1 (not_1_out, State[2]);
  not not_2 (not_2_out, State[1]);
  not not_3 (not_3_out, State[0]);
  and and_1 (and_1_out, State[2], not_2_out, not_3_out);
  and and_2 (and_2_out, State[2], State[1], State[0]);
  and and_3 (and_3_out, not_1_out, State[1], State[0]);
  and and_4 (and_4_out, State[2], not_2_out, State[0]);
  and and_5 (and_5_out, State[2], State[1], not_3_out);
  and and_6 (and_6_out, not_1_out, State[1], State[0]);
  and and_7 (and_7_out, State[2], not_2_out, State[0]);
  and and_8 (and_8_out, State[2], State[1], not_3_out);
  and and_9 (ready, not_1_out, not_2_out, State[0]);
  and and_10 (init, not_1_out, not_2_out, not_3_out);
  and and_11 (and_11_out, not_1_out, not_3_out);
  and and_12 (and_12_out, not_1_out, State[1]);
  and and_13 (and_13_out, State[2], not_2_out);
  and and_14 (WriteByteFromCPUWrite, State[2], not_2_out, State[0]);
  or or_1 (memWrite, and_1_out, and_2_out);
  or or_2 (memRead, and_3_out, and_4_out, and_5_out);
  or or_3 (writeByte, and_6_out, and_7_out, and_8_out);
  or or_4 (updateAge, and_11_out, and_12_out, and_13_out);
endmodule
