// Logisim project FourBitParity.circ as structural Verilog: 3 circuits, main circuit implementation
module implementation (
  input  EnableIn,
  input  InputBitIn,
  input  ClkIn,
  output IsEvenOut
);

  wire [3:0] nextstate_1_s0_next, register_1_q;

  NextState nextstate_1 (
    .s3(register_1_q[3]), .s2(register_1_q[2]), .s1(register_1_q[1]), .s0(register_1_q[0]),
    .InputBits(InputBitIn), .s3_next(nextstate_1_s0_next[3]), .s2_next(nextstate_1_s0_next[2]),
    .s1_next(nextstate_1_s0_next[1]), .s0_next(nextstate_1_s0_next[0]));
  Register #(.width(4)) register_1 (
    .D(nextstate_1_s0_next), .en(EnableIn), .clk(ClkIn), .Q(register_1_q));  // open: clr
  BitOutput bitoutput_1 (
    .S3(register_1_q[3]), .S2(register_1_q[2]), .S1(register_1_q[1]), .s0(register_1_q[0]), .BitOut(IsEvenOut));

  // Other names for the same wires on the sheet: Clk = ClkIn; Enable = EnableIn; InputBit = InputBitIn
endmodule

module NextState (
  input  s3,
  input  s2,
  input  s1,
  input  s0,
  input  InputBits,
  output s3_next,
  output s2_next,
  output s1_next,
  output s0_next
);

  wire and_1_out, and_2_out, and_3_out, and_4_out, and_5_out, and_6_out, and_7_out, and_8_out, and_9_out,
       and_10_out, and_11_out, and_12_out, and_13_out, and_14_out, and_15_out, and_16_out, and_17_out,
       and_18_out, not_1_out, not_2_out, not_3_out, not_4_out, not_5_out;

  not not_1 (not_1_out, s3);
  not not_2 (not_2_out, s2);
  not not_3 (not_3_out, s1);
  not not_4 (not_4_out, s0);
  not not_5 (not_5_out, InputBits);
  and and_1 (and_1_out, s2, s1, not_4_out, not_5_out);
  and and_2 (and_2_out, s2, s1, s0, InputBits);
  and and_3 (and_3_out, s3, s1, not_4_out, not_5_out);
  and and_4 (and_4_out, s3, s2, not_4_out, not_5_out);
  and and_5 (and_5_out, s3, s2, s0, InputBits);
  and and_6 (and_6_out, not_2_out, s1);
  and and_7 (and_7_out, not_1_out, s2, not_3_out);
  and and_8 (and_8_out, s2, not_3_out, s0, not_5_out);
  and and_9 (and_9_out, not_1_out, not_3_out);
  and and_10 (and_10_out, not_2_out, not_3_out, not_4_out);
  and and_11 (and_11_out, s2, not_3_out, s0, not_5_out);
  and and_12 (and_12_out, not_1_out, not_2_out, not_3_out, InputBits);
  and and_13 (and_13_out, not_1_out, not_4_out, InputBits);
  and and_14 (and_14_out, not_2_out, not_4_out, InputBits);
  and and_15 (and_15_out, not_1_out, s1, s0, not_5_out);
  and and_16 (and_16_out, s2, s0, not_5_out);
  and and_17 (and_17_out, s3, not_2_out, s1, not_4_out);
  and and_18 (and_18_out, s3, s2, not_3_out, not_5_out);
  or or_1 (s3_next, and_1_out, and_2_out, and_3_out, and_4_out, and_5_out);
  or or_2 (s2_next, and_6_out, and_7_out, and_8_out);
  or or_3 (s1_next, and_9_out, and_10_out, and_11_out);
  or or_4 (s0_next, and_12_out, and_13_out, and_14_out, and_15_out, and_16_out, and_17_out, and_18_out);
endmodule

module BitOutput (
  input  S3,
  input  S2,
  input  S1,
  input  s0,
  output BitOut
);


  assign BitOut = S3;
endmodule
