// Logisim project UpDownCounter.circ as structural Verilog: 2 circuits, main circuit implementation
module implementation (
  input  EnableIn,
  input  CountUpIn,
  input  CountDownIn,
  input  clkIn,
  output [2:0] Count
);

  wire [2:0] nextstate_1_s0_next;

  NextState nextstate_1 (
    .s2(Count[2]), .s1(Count[1]), .s0(Count[0]), .PlusOne(CountUpIn), .MinusOne(CountDownIn),
    .s2_next(nextstate_1_s0_next[2]), .s1_next(nextstate_1_s0_next[1]), .s0_next(nextstate_1_s0_next[0]));
  Register #(.width(3)) register_1 (.D(nextstate_1_s0_next), .en(EnableIn), .clk(clkIn), .Q(Count));  // open: clr

  // Other names for the same wires on the sheet: clk = clkIn; CountDown = CountDownIn; CountUp = CountUpIn;
  //   Enable = EnableIn
endmodule

module NextState (
  input  s2,
  input  s1,
  input  s0,
  input  PlusOne,
  input  MinusOne,
  output s2_next,
  output s1_next,
  output s0_next
);

  wire and_1_out, and_2_out, and_3_out, and_4_out, and_5_out, and_6_out, and_7_out, and_8_out, and_9_out,
       and_10_out, and_11_out, and_12_out, and_13_out, and_14_out, not_1_out, not_2_out, not_3_out, not_4_out;

  not not_1 (not_1_out, s1);
  not not_2 (not_2_out, s0);
  not not_3 (not_3_out, PlusOne);
  not not_4 (not_4_out, MinusOne);
  and and_1 (and_1_out, s1, s0, PlusOne);
  and and_2 (and_2_out, s2, not_4_out);
  and and_3 (and_3_out, s2, s0);
  and and_4 (and_4_out, s2, s1);
  and and_5 (and_5_out, not_1_out, s0, PlusOne);
  and and_6 (and_6_out, s1, not_2_out, not_4_out);
  and and_7 (and_7_out, s1, s0, not_3_out);
  and and_8 (and_8_out, s2, not_1_out, not_2_out, MinusOne);
  and and_9 (and_9_out, s2, s1, not_4_out);
  and and_10 (and_10_out, not_2_out, PlusOne);
  and and_11 (and_11_out, s0, not_3_out, not_4_out);
  and and_12 (and_12_out, s1, not_2_out, MinusOne);
  and and_13 (and_13_out, s2, not_2_out, MinusOne);
  and and_14 (and_14_out, s2, s1, s0, not_4_out);
  or or_1 (s2_next, and_1_out, and_2_out, and_3_out, and_4_out);
  or or_2 (s1_next, and_5_out, and_6_out, and_7_out, and_8_out, and_9_out);
  or or_3 (s0_next, and_10_out, and_11_out, and_12_out, and_13_out, and_14_out);
endmodule
