// Logisim project Vending.circ as structural Verilog: 3 circuits, main circuit implementation
module implementation (
  input  EnableIn,
  input  QuarterReceivedIn,
  input  DimeReceivedIn,
  input  NickelReceivedIn,
  input  ClkIn,
  output Give_Mechandise_Out,
  output Give_Dime_Out,
  output Give_Nickel_Out
);

  wire [2:0] nextstate_1_s0_next, register_1_q;

  NextState nextstate_1 (
    .s2(register_1_q[2]), .s1(register_1_q[1]), .s0(register_1_q[0]), .q_in(QuarterReceivedIn),
    .d_in(DimeReceivedIn), .n_in(NickelReceivedIn), .s2_next(nextstate_1_s0_next[2]),
    .s1_next(nextstate_1_s0_next[1]), .s0_next(nextstate_1_s0_next[0]));
  Register #(.width(3)) register_1 (
    .D(nextstate_1_s0_next), .en(EnableIn), .clk(ClkIn), .Q(register_1_q));  // open: clr
  BitOut bitout_1 (
    .s2(register_1_q[2]), .s1(register_1_q[1]), .s0(register_1_q[0]), .q_in(QuarterReceivedIn),
    .d_in(DimeReceivedIn), .n_in(NickelReceivedIn), .d_out(Give_Dime_Out), .n_out(Give_Nickel_Out),
    .m_out(Give_Mechandise_Out));

  // Other names for the same wires on the sheet: clk = ClkIn; DimeReceieved = DimeReceivedIn; Enable = EnableIn;
  //   Give_Dime = Give_Dime_Out; Give_Merchandise = Give_Mechandise_Out; Give_Nickel = Give_Nickel_Out;
  //   NickelReceieved = NickelReceivedIn; QuarterReceieved = QuarterReceivedIn
endmodule

module NextState (
  input  s2,
  input  s1,
  input  s0,
  input  q_in,
  input  d_in,
  input  n_in,
  output s2_next,
  output s1_next,
  output s0_next
);

  wire and_1_out, and_2_out, and_3_out, and_4_out, and_5_out, and_6_out, and_7_out, and_8_out, and_9_out,
       and_10_out, and_11_out, and_12_out, and_13_out, not_1_out, not_2_out, not_3_out, not_4_out, not_5_out,
       not_6_out;

  not not_1 (not_1_out, s2);
  not not_2 (not_2_out, s1);
  not not_3 (not_3_out, s0);
  not not_4 (not_4_out, q_in);
  not not_5 (not_5_out, d_in);
  not not_6 (not_6_out, n_in);
  and and_1 (and_1_out, not_1_out, not_2_out, not_3_out, q_in);
  and and_2 (and_2_out, s1, d_in);
  and and_3 (and_3_out, s1, s0, n_in);
  and and_4 (and_4_out, s2, not_2_out, not_4_out, not_5_out, not_6_out);
  and and_5 (and_5_out, s2, not_3_out, not_4_out, not_5_out);
  and and_6 (and_6_out, not_1_out, not_2_out, d_in);
  and and_7 (and_7_out, not_1_out, not_2_out, s0, n_in);
  and and_8 (and_8_out, s1, not_4_out, not_5_out, not_6_out);
  and and_9 (and_9_out, s1, not_3_out, n_in);
  and and_10 (and_10_out, not_3_out, n_in);
  and and_11 (and_11_out, not_1_out, not_2_out, not_3_out, q_in);
  and and_12 (and_12_out, not_1_out, s0, not_4_out, not_6_out);
  and and_13 (and_13_out, not_2_out, s0, not_4_out, not_5_out, not_6_out);
  or or_1 (s2_next, and_1_out, and_2_out, and_3_out, and_4_out, and_5_out);
  or or_2 (s1_next, and_6_out, and_7_out, and_8_out, and_9_out);
  or or_3 (s0_next, and_10_out, and_11_out, and_12_out, and_13_out);
endmodule

module BitOut (
  input  s2,
  input  s1,
  input  s0,
  input  q_in,
  input  d_in,
  input  n_in,
  output d_out,
  output n_out,
  output m_out
);

  wire and_1_out, and_2_out, and_3_out, and_4_out, and_5_out, and_6_out, and_7_out, and_8_out, and_9_out,
       and_10_out, not_1_out;

  not not_1 (not_1_out, s0);
  and and_1 (and_1_out, s1, s0, q_in);
  and and_2 (and_2_out, s2, q_in);
  and and_3 (and_3_out, s1, not_1_out, q_in);
  and and_4 (and_4_out, s2, q_in);
  and and_5 (and_5_out, s2, s0, d_in);
  and and_6 (and_6_out, s0, q_in);
  and and_7 (and_7_out, s1, q_in);
  and and_8 (and_8_out, s2, d_in);
  and and_9 (and_9_out, s2, q_in);
  and and_10 (and_10_out, s2, s0, n_in);
  or or_1 (d_out, and_1_out, and_2_out);
  or or_2 (n_out, and_3_out, and_4_out, and_5_out);
  or or_3 (m_out, and_6_out, and_7_out, and_8_out, and_9_out, and_10_out);
endmodule
