// Logisim project adder4.circ as structural Verilog: 5 circuits, main circuit implementation
module implementation (
  input  [3:0] Ain,
  input  [3:0] Bin,
  input  Cinin,
  output [3:0] Sum_Out,
  output Carry_Out
);

  wire C0out, C1out, C2out, G0, G1, G2, G3, P0, P1, P2, P3;

  and and_1 (G0, Ain[0], Bin[0]);
  and and_2 (G1, Ain[1], Bin[1]);
  and and_3 (G2, Ain[2], Bin[2]);
  and and_4 (G3, Ain[3], Bin[3]);
  xor xor_1 (P0, Ain[0], Bin[0]);
  xor xor_2 (P1, Ain[1], Bin[1]);
  xor xor_3 (P2, Ain[2], Bin[2]);
  xor xor_4 (P3, Ain[3], Bin[3]);
  C0 c0_1 (.G0(G0), .P0(P0), .Cin(Cinin), .Cout(C0out));
  C1 c1_1 (.G1in(G1), .P1in(P1), .G0in(G0), .P0in(P0), .Cinin(Cinin), .C1out(C1out));
  C2 c2_1 (.G2in(G2), .G1in(G1), .G0in(G0), .P2in(P2), .P1in(P1), .P0in(P0), .Cinin(Cinin), .C2out(C2out));
  C3 c3_1 (
    .G3in(G3), .G2in(G2), .G1in(G1), .G0in(G0), .P3in(P3), .P2in(P2), .P1in(P1), .P0in(P0), .Cinin(Cinin),
    .C3out(Carry_Out));
  xor xor_5 (Sum_Out[0], P0, Cinin);
  xor xor_6 (Sum_Out[1], P1, C0out);
  xor xor_7 (Sum_Out[2], P2, C1out);
  xor xor_8 (Sum_Out[3], P3, C2out);

  // Other names for the same wires on the sheet: A[3:0] = Ain; A0 = Ain[0]; A1 = Ain[1]; A2 = Ain[2]; A3 = Ain[3];
  //   B[3:0] = Bin; B0 = Bin[0]; B1 = Bin[1]; B2 = Bin[2]; B3 = Bin[3]; C3out = Carry_Out; Cin = Cinin;
  //   Sum[3:0] = Sum_Out; sum0 = Sum_Out[0]; sum1 = Sum_Out[1]; sum2 = Sum_Out[2]; sum3 = Sum_Out[3]
endmodule

module C0 (
  input  G0,
  input  P0,
  input  Cin,
  output Cout
);

  wire and_1_out;

  or or_1 (Cout, G0, and_1_out);
  and and_1 (and_1_out, P0, Cin);
endmodule

module C1 (
  input  G1in,
  input  P1in,
  input  G0in,
  input  P0in,
  input  Cinin,
  output C1out
);

  wire and_1_out, and_2_out, and_3_out;

  and and_1 (and_1_out, P1in, G0in);
  and and_2 (and_2_out, P1in, P0in);
  and and_3 (and_3_out, and_2_out, Cinin);
  or or_1 (C1out, G1in, and_1_out, and_3_out);

  // Other names for the same wires on the sheet: Cin = Cinin; G0 = G0in; G1 = G1in; P0 = P0in; P1 = P1in
endmodule

module C2 (
  input  G2in,
  input  G1in,
  input  G0in,
  input  P2in,
  input  P1in,
  input  P0in,
  input  Cinin,
  output C2out
);

  wire and_1_out, and_2_out, and_3_out, and_4_out;

  and and_1 (and_1_out, P2in, G1in);
  and and_2 (and_2_out, P2in, P1in, G0in);
  and and_3 (and_3_out, P2in, P1in, P0in);
  and and_4 (and_4_out, and_3_out, Cinin);
  or or_1 (C2out, G2in, and_1_out, and_2_out, and_4_out);

  // Other names for the same wires on the sheet: Cin = Cinin; G0 = G0in; G1 = G1in; G2 = G2in; P0 = P0in; P1 = P1in;
  //   P2 = P2in
endmodule

module C3 (
  input  G3in,
  input  G2in,
  input  G1in,
  input  G0in,
  input  P3in,
  input  P2in,
  input  P1in,
  input  P0in,
  input  Cinin,
  output C3out
);

  wire and_1_out, and_2_out, and_3_out, and_4_out, and_5_out;

  and and_1 (and_1_out, P3in, G2in);
  and and_2 (and_2_out, P3in, P2in, G1in);
  and and_3 (and_3_out, P3in, P2in, P1in, G0in);
  and and_4 (and_4_out, P3in, P2in, P1in, P0in);
  and and_5 (and_5_out, and_4_out, Cinin);
  or or_1 (C3out, G3in, and_1_out, and_2_out, and_3_out, and_5_out);

  // Other names for the same wires on the sheet: Cin = Cinin; G0 = G0in; G1 = G1in; G2 = G2in; G3 = G3in; P0 = P0in;
  //   P1 = P1in; P2 = P2in; P3 = P3in
endmodule
