// Logisim project bcd.circ as structural Verilog: 1 circuit, main circuit implementation
module implementation (
  input  w3,
  input  w2,
  input  w1,
  input  w0,
  output a,
  output b,
  output c,
  output d,
  output e,
  output f,
  output g
);

  wire and_1_out, and_2_out, and_3_out, and_4_out, and_5_out, and_6_out, and_7_out, and_8_out, and_9_out,
       and_10_out, and_11_out, and_12_out, and_13_out, and_14_out, not_1_out, not_2_out, not_3_out,
       not_4_out, not_5_out, not_6_out, not_7_out, not_8_out, not_9_out, not_10_out, not_11_out, not_12_out,
       not_13_out, not_14_out, not_15_out, not_16_out, not_17_out, not_18_out, not_19_out, or_1_out,
       or_2_out, or_3_out, or_4_out, xor_1_out;

  not not_1 (not_1_out, w1);
  not not_2 (not_2_out, w0);
  not not_3 (not_3_out, w0);
  not not_4 (not_4_out, w1);
  not not_5 (not_5_out, w2);
  not not_6 (not_6_out, w0);
  and and_1 (and_1_out, not_1_out, w0);
  and and_2 (and_2_out, not_2_out, w1);
  or or_1 (or_1_out, not_3_out, w1);
  not not_7 (not_7_out, w2);
  or or_2 (or_2_out, w0, w1);
  xor xor_1 (xor_1_out, w0, not_4_out);
  or or_3 (or_3_out, not_6_out, w1);
  not not_8 (not_8_out, w2);
  or or_4 (or_4_out, and_1_out, and_2_out);
  and and_3 (and_3_out, or_1_out, not_7_out);
  and and_4 (and_4_out, or_2_out, w2);
  or or_5 (b, xor_1_out, not_5_out);
  and and_5 (and_5_out, or_3_out, not_8_out);
  and and_6 (and_6_out, or_4_out, w2);
  or or_6 (a, and_3_out, w3, and_4_out);
  or or_7 (d, and_5_out, w3, and_6_out);
  not not_9 (not_9_out, w1);
  not not_10 (not_10_out, w2);
  not not_11 (not_11_out, w0);
  not not_12 (not_12_out, w0);
  not not_13 (not_13_out, w1);
  not not_14 (not_14_out, w0);
  not not_15 (not_15_out, w0);
  not not_16 (not_16_out, w1);
  not not_17 (not_17_out, w2);
  not not_18 (not_18_out, w0);
  not not_19 (not_19_out, w1);
  or or_8 (c, w3, w2, w0, not_9_out);
  and and_7 (and_7_out, not_10_out, not_11_out);
  and and_8 (and_8_out, not_12_out, w1);
  and and_9 (and_9_out, not_13_out, not_14_out);
  and and_10 (and_10_out, not_15_out, w2);
  and and_11 (and_11_out, not_16_out, w2);
  and and_12 (and_12_out, not_17_out, w1);
  and and_13 (and_13_out, not_18_out, w2);
  and and_14 (and_14_out, not_19_out, w2);
  or or_9 (e, and_7_out, and_8_out);
  or or_10 (f, and_9_out, and_10_out, and_11_out, w3);
  or or_11 (g, and_12_out, and_13_out, and_14_out, w3);

  // Other names for the same wires on the sheet: at = a; bt = b; ct = c; dt = d; et = e; ft = f; gt = g; w0t = w0;
  //   w1t = w1; w2t = w2; w3t = w3
endmodule
