// Logisim project bitcounter.circ as structural Verilog: 5 circuits, main circuit implementation
module implementation (
  input  [7:0] BitsIn,
  input  CountZerosIn,
  output [3:0] BitCountOut
);

  wire Bout;
  wire [1:0] tot1s1, tot1s2, tot1s3, tot1s4;
  wire [2:0] tot2s1, tot2s2;
  wire [3:0] oneCount, zeroCount;

  // Probe on tot1s1
  twobitcounter twobitcounter_1 (.Ain(BitsIn[0]), .Bin(BitsIn[1]), .Cin_always0(1'b0), .out2(tot1s1));
  // Probe on tot1s2
  twobitcounter twobitcounter_2 (.Ain(BitsIn[2]), .Bin(BitsIn[3]), .Cin_always0(1'b0), .out2(tot1s2));
  // Probe on tot1s3
  twobitcounter twobitcounter_3 (.Ain(BitsIn[4]), .Bin(BitsIn[5]), .Cin_always0(1'b0), .out2(tot1s3));
  // Probe on tot1s4
  twobitcounter twobitcounter_4 (.Ain(BitsIn[6]), .Bin(BitsIn[7]), .Cin_always0(1'b0), .out2(tot1s4));
  // Probe on tot2s1
  twobittothree twobittothree_1 (.Cin_always0(1'b0), .sumA(tot1s1), .sumB(tot1s2), .sumout(tot2s1));
  // Probe on tot2s2
  twobittothree twobittothree_2 (.Cin_always0(1'b0), .sumA(tot1s3), .sumB(tot1s4), .sumout(tot2s2));
  Multiplexer #(.enable("false"), .width(4)) multiplexer_1 (
    .in0(oneCount), .in1(zeroCount), .out(BitCountOut), .sel(CountZerosIn));
  // Probe on BitCountOut
  // Probe on oneCount
  // Probe on zeroCount
  threebittofour threebittofour_1 (.CinAlways0(1'b0), .Ain(tot2s1), .Bin(tot2s2), .sumout(oneCount));
  zeros zeros_1 (.BinAlways0(1'b0), .in8(4'b1000), .numOnes(oneCount), .Out0s(zeroCount), .BoutDoesntMatter(Bout));

  // Other names for the same wires on the sheet: BitCount[3:0] = BitCountOut; B0 = BitsIn[0]; Bits[7:0] = BitsIn;
  //   B1 = BitsIn[1]; B2 = BitsIn[2]; B3 = BitsIn[3]; B4 = BitsIn[4]; B5 = BitsIn[5]; B6 = BitsIn[6]; B7 = BitsIn[7];
  //   CountZeros = CountZerosIn
endmodule

module twobitcounter (
  input  Ain,
  input  Bin,
  input  Cin_always0,
  output [1:0] out2
);

  wire and_1_out, and_2_out, and_3_out;

  ExactlyOne xor_1 (.out(out2[0]), .in0(Ain), .in1(Bin), .in2(Cin_always0));
  and and_1 (and_1_out, Ain, Bin);
  and and_2 (and_2_out, Ain, Cin_always0);
  and and_3 (and_3_out, Bin, Cin_always0);
  or or_1 (out2[1], and_1_out, and_2_out, and_3_out);
  // Probe on out2

  // Other names for the same wires on the sheet: A = Ain; B = Bin; Cin = Cin_always0; sum = out2[0]; Cout = out2[1]
endmodule

module twobittothree (
  input  Cin_always0,
  input  [1:0] sumA,
  input  [1:0] sumB,
  output [2:0] sumout
);

  Adder #(.width(2)) adder_1 (.a(sumA), .b(sumB), .out(sumout[1:0]), .cin(Cin_always0), .cout(sumout[2]));

  // Other names for the same wires on the sheet: bit1 = sumout[0]; sum[1:0] = sumout[1:0]; bit2 = sumout[1];
  //   carryout = sumout[2]
endmodule

module threebittofour (
  input  CinAlways0,
  input  [2:0] Ain,
  input  [2:0] Bin,
  output [3:0] sumout
);

  Adder #(.width(3)) adder_1 (.a(Ain), .b(Bin), .out(sumout[2:0]), .cin(CinAlways0), .cout(sumout[3]));

  // Other names for the same wires on the sheet: s1 = sumout[0]; sum[2:0] = sumout[2:0]; s2 = sumout[1];
  //   s3 = sumout[2]; Cout = sumout[3]
endmodule

module zeros (
  input  BinAlways0,
  input  [3:0] in8,
  input  [3:0] numOnes,
  output [3:0] Out0s,
  output BoutDoesntMatter
);

  // Probe on in8
  // Probe on numOnes
  Subtractor #(.width(4)) subtractor_1 (.a(in8), .b(numOnes), .out(Out0s), .bin(BinAlways0), .bout(BoutDoesntMatter));
  // Probe on Out0s
endmodule
