// Logisim project shifter.circ as structural Verilog: 7 circuits, main circuit implementation
module implementation (
  input  IsRightShiftIn,
  input  IsArithmeticIn,
  input  [1:0] ShiftAmountIn,
  input  [2:0] NumberIn,
  output [2:0] ShiftedNumberOut
);

  wire [2:0] ArithmeticShift, GeometricShift;

  Multiplexer #(.enable("false"), .width(3)) multiplexer_1 (
    .in0(GeometricShift), .in1(ArithmeticShift), .out(ShiftedNumberOut), .sel(IsArithmeticIn));
  ArithmeticShifter arithmeticshifter_1 (
    .RightShift(IsRightShiftIn), .Amount(ShiftAmountIn), .NumToShift(NumberIn),
    .ShiftedOutput(ArithmeticShift));
  GeometricShifter geometricshifter_1 (
    .RightShift(IsRightShiftIn), .Amount(ShiftAmountIn), .NumToShift(NumberIn), .ShiftedOutput(GeometricShift));

  // Other names for the same wires on the sheet: IsArithmetic = IsArithmeticIn; IsRightShift = IsRightShiftIn;
  //   Number[2:0] = NumberIn; ShiftAmount[1:0] = ShiftAmountIn; ShiftedNumber[2:0] = ShiftedNumberOut
endmodule

module ArithmeticShifter (
  input  RightShift,
  input  [1:0] Amount,
  input  [2:0] NumToShift,
  output [2:0] ShiftedOutput
);

  wire [2:0] ShiftedLeft, ShiftedRight;

  AR ar_1 (.Amount(Amount), .NumToShift(NumToShift), .Result(ShiftedRight));
  AL al_1 (.Amount(Amount), .NumToShift(NumToShift), .Result(ShiftedLeft));
  // Probe on ShiftedOutput
  Multiplexer #(.enable("false"), .width(3)) multiplexer_1 (
    .in0(ShiftedLeft), .in1(ShiftedRight), .out(ShiftedOutput), .sel(RightShift));

  // Other names for the same wires on the sheet: IsRight = RightShift; Num[2:0] = NumToShift;
  //   ShiftAmount[1:0] = Amount
endmodule

module GeometricShifter (
  input  RightShift,
  input  [1:0] Amount,
  input  [2:0] NumToShift,
  output [2:0] ShiftedOutput
);

  wire [2:0] ShiftedLeft, ShiftedRight;

  GR gr_1 (.Amount(Amount), .NumToShift(NumToShift), .Result(ShiftedRight));
  GL gl_1 (.Amount(Amount), .NumToShift(NumToShift), .Result(ShiftedLeft));
  // Probe on ShiftedOutput
  Multiplexer #(.enable("false"), .width(3)) multiplexer_1 (
    .in0(ShiftedLeft), .in1(ShiftedRight), .out(ShiftedOutput), .sel(RightShift));

  // Other names for the same wires on the sheet: IsRight = RightShift; Num[2:0] = NumToShift;
  //   ShiftAmount[1:0] = Amount
endmodule

module AR (
  input  [1:0] Amount,
  input  [2:0] NumToShift,
  output [2:0] Result
);

  // Probe on NumToShift
  // Probe on {3{NumToShift[2]}}
  // Probe on {3{NumToShift[2]}}
  // Probe on {{2{NumToShift[2]}}, NumToShift[1]}
  // Probe on NumToShift
  // Probe on Result
  Multiplexer #(.enable("false"), .select(2), .width(3)) multiplexer_1 (
    .in0(NumToShift), .in1({{2{NumToShift[2]}}, NumToShift[1]}), .in2({3{NumToShift[2]}}),
    .in3({3{NumToShift[2]}}), .out(Result), .sel(Amount));

  // Other names for the same wires on the sheet: ShiftAmount[1:0] = Amount; ShiftBit0 = Amount[0];
  //   ShiftBit1 = Amount[1]; Bit0 = NumToShift[0]; Num[2:0] = NumToShift; Shift0[2:0] = NumToShift;
  //   Bit1 = NumToShift[1]; Shift1[2:0] = {{2{NumToShift[2]}}, NumToShift[1]}; Bit2 = NumToShift[2];
  //   Shift2[2:0] = {3{NumToShift[2]}}; Shift3[2:0] = {3{NumToShift[2]}}; ShiftedRight[2:0] = Result
endmodule

module AL (
  input  [1:0] Amount,
  input  [2:0] NumToShift,
  output [2:0] Result
);

  // Probe on NumToShift
  // Probe on 3'b000
  // Probe on {NumToShift[0], 2'b00}
  // Probe on {NumToShift[1:0], 1'b0}
  // Probe on NumToShift
  // Probe on Result
  Multiplexer #(.enable("false"), .select(2), .width(3)) multiplexer_1 (
    .in0(NumToShift), .in1({NumToShift[1:0], 1'b0}), .in2({NumToShift[0], 2'b00}), .in3(3'b000),
    .out(Result), .sel(Amount));

  // Other names for the same wires on the sheet: ShiftAmount[1:0] = Amount; ShiftBit0 = Amount[0];
  //   ShiftBit1 = Amount[1]; Bit0 = NumToShift[0]; Num[2:0] = NumToShift; Shift0[2:0] = NumToShift;
  //   Shift1[2:1] = NumToShift[1:0]; Shift2[2] = NumToShift[0]; Bit1 = NumToShift[1]; Bit2 = NumToShift[2];
  //   ShiftedRight[2:0] = Result
endmodule

module GR (
  input  [1:0] Amount,
  input  [2:0] NumToShift,
  output [2:0] Result
);

  // Probe on NumToShift
  // Probe on 3'b000
  // Probe on {2'b00, NumToShift[2]}
  // Probe on {1'b0, NumToShift[2:1]}
  // Probe on NumToShift
  // Probe on Result
  Multiplexer #(.enable("false"), .select(2), .width(3)) multiplexer_1 (
    .in0(NumToShift), .in1({1'b0, NumToShift[2:1]}), .in2({2'b00, NumToShift[2]}), .in3(3'b000),
    .out(Result), .sel(Amount));

  // Other names for the same wires on the sheet: ShiftAmount[1:0] = Amount; ShiftBit0 = Amount[0];
  //   ShiftBit1 = Amount[1]; Bit0 = NumToShift[0]; Num[2:0] = NumToShift; Shift0[2:0] = NumToShift;
  //   Bit1 = NumToShift[1]; Shift1[1:0] = NumToShift[2:1]; Bit2 = NumToShift[2]; Shift2[0] = NumToShift[2];
  //   ShiftedRight[2:0] = Result
endmodule

module GL (
  input  [1:0] Amount,
  input  [2:0] NumToShift,
  output [2:0] Result
);

  // Probe on NumToShift
  // Probe on 3'b000
  // Probe on {NumToShift[0], 2'b00}
  // Probe on {NumToShift[1:0], 1'b0}
  // Probe on NumToShift
  // Probe on Result
  Multiplexer #(.enable("false"), .select(2), .width(3)) multiplexer_1 (
    .in0(NumToShift), .in1({NumToShift[1:0], 1'b0}), .in2({NumToShift[0], 2'b00}), .in3(3'b000),
    .out(Result), .sel(Amount));

  // Other names for the same wires on the sheet: ShiftAmount[1:0] = Amount; ShiftBit0 = Amount[0];
  //   ShiftBit1 = Amount[1]; Bit0 = NumToShift[0]; Num[2:0] = NumToShift; Shift0[2:0] = NumToShift;
  //   Shift1[2:1] = NumToShift[1:0]; Shift2[2] = NumToShift[0]; Bit1 = NumToShift[1]; Bit2 = NumToShift[2];
  //   ShiftedRight[2:0] = Result
endmodule
